# Fritzing sketch wiring (saved by Fritzing 0.9.3b)
breadboards: 1

parts:
  Part1 = Arduino Uno (Rev3)
  U1 = LCD-16X2 [package=lcd-16x2_noholes]
  R1 = Resistor [tolerance=±5% resistance=5k package=THT]

nets:
  N1: Part1.D8, U1.E
  N2: Part1.D9_PWM, U1.DB4
  N3: Part1.D10_PWM/SS, U1.DB5
  N4: Part1.D11_PWM/MOSI, U1.DB6
  N5: Part1.D12/MISO, U1.DB7
  N6: Part1.D7, U1.RS
  5V: Part1.5V, U1.VDD, U1.A
  GND: Part1.GND, U1.VSS, U1.R_W, U1.K, R1.Pin_0
  N7: U1.VO, R1.Pin_1
